// Logisim project NOR_NOTANDORR.circ as structural Verilog: 1 circuit, main circuit main
module main (
  input  A,
  input  B,
  output NOT,
  output AND,
  output OR
);

  wire nor_2_out, nor_3_out, nor_4_out;

  nor nor_1 (NOT, A, 1'b0);
  nor nor_2 (nor_2_out, A, 1'b0);
  nor nor_3 (nor_3_out, 1'b0, B);
  nor nor_4 (nor_4_out, B, A);
  nor nor_5 (AND, nor_2_out, nor_3_out);
  nor nor_6 (OR, nor_4_out, 1'b0);
endmodule
