// Logisim project NOR_OR.circ as structural Verilog: 1 circuit, main circuit main
module main (
  input  A,
  input  B,
  output OR
);

  wire nor_1_out;

  nor nor_1 (nor_1_out, A, B);
  nor nor_2 (OR, nor_1_out, 1'b0);
endmodule
